# Fritzing sketch fritzing (saved by Fritzing 0.9.5d)
breadboards: 1

parts:
  R4 = Resistor [tolerance=±1% resistance=2.2k package=THT]
  抵抗内蔵LED(5V)1 = smd LED [color="Red (633nm)" package="0603 [SMD]"]
  NchパワーMOSFET_60V5A_2SK4017 = Basic FET N-Channel [package="D2Pak [SMD]"]
  抵抗内蔵LED(5V)2 = smd LED [color="Red (633nm)" package="0603 [SMD]"]
  R3 = Resistor [tolerance=±1% resistance=220k package=THT]
  Raspberry_Pi_Pico_WH = Raspberry Pi Pico H
  S2 = Pushbutton [package="[THT]"]
  NchパワーMOSFET_60V5A_2SK4018 = Basic FET N-Channel [package="D2Pak [SMD]"]
  R5 = Resistor [tolerance=±1% resistance=220k package=THT]
  R6 = Resistor [tolerance=±1% resistance=2.2k package=THT]
  パーツ2 = Arduino Nano Every  # not connected

nets:
  N1: R4.Pin_0, Raspberry_Pi_Pico_WH.GP17
  N2: R4.Pin_1, NchパワーMOSFET_60V5A_2SK4017.Gate, R5.Pin_0
  N3: 抵抗内蔵LED(5V)1.cathode, NchパワーMOSFET_60V5A_2SK4018.drain
  N4: 抵抗内蔵LED(5V)1.anode, 抵抗内蔵LED(5V)2.anode, Raspberry_Pi_Pico_WH.VBUS
  N5: NchパワーMOSFET_60V5A_2SK4017.drain, 抵抗内蔵LED(5V)2.cathode
  N6: NchパワーMOSFET_60V5A_2SK4017.source, R3.Pin_1, Raspberry_Pi_Pico_WH.GND, NchパワーMOSFET_60V5A_2SK4018.source, R5.Pin_1
  N7: R3.Pin_0, NchパワーMOSFET_60V5A_2SK4018.Gate, R6.Pin_1
  N8: Raspberry_Pi_Pico_WH.3V3, S2.Pin_3, S2.Pin_4
  N9: Raspberry_Pi_Pico_WH.GP16, R6.Pin_0
  N10: Raspberry_Pi_Pico_WH.GP15, S2.Pin_1, S2.Pin_2

custom parts:
  Raspberry Pi Pico H: Raspberry Pi Pico H. Based around the RP2040 microcontroller the Pico H is a low cost microcontroller device bringing Raspberry Pi quality, cost, and easy of use to the microcontroller space.
  Arduino Nano Every: The Nano Every is Arduino’s 5V compatible board in the smallest available form factor: 45x18mm! The Arduino Nano is the preferred board for many projects requiring a small and easy to use microcontroller board. The small footprint and low price, make the Nano Every particularly suited for wearable inventions, low cost robotics, electronic musical instruments, and general use to control smaller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
